# Fritzing sketch AntiBueeBMP (saved by Fritzing 0.9.3b)
stripboards: 2

parts:
  WeMos_D1_Mini1 = WeMos D1 Mini
  Composant1 = InvenSense MPU6050
  Alimentation_5_0_12V = Camdenboss CTB0158-3 [part_number=CTB0158-3 package=THT]
  12V_caméra = Camdenboss CTB0158-2 [part_number=CTB0158-2 package=THT]
  12V_chauffage = Camdenboss CTB0158-2 [part_number=CTB0158-2 package=THT]
  1wire = female pin header, 2 pins [form="♀ (female)"]
  MPU6050 = female pin header, 8 pins [form="♀ (female)"]
  R1 = Resistor [tolerance=±5% resistance=6.8k package="0805 [SMD]"]
  Park = female alternating pin header, 3 pins [form="♀ (female)"]
  J6 = female pin header, 8 pins [form="♀ (female)"]
  J7 = female pin header, 8 pins [form="♀ (female)"]
  BME280 = female pin header, 4 pins [form="♀ (female)"]
  LED = female pin header, 2 pins [form="♀ (female)"]
  Q1 = MOSFET-NCHANNEL [package=to220v]
  R2 = Resistor [tolerance=±5% resistance=1k package="0805 [SMD]"]
  Composant2 = Logic Level Converter
  Composant3 = Arduino Nano (Rev3.0) (ICSP)
  Alimentation_5_0_12V1 = Camdenboss CTB0158-3 [part_number=CTB0158-3 package=THT]
  12V_chauffage1 = Camdenboss CTB0158-2 [part_number=CTB0158-2 package=THT]
  12V_caméra1 = Camdenboss CTB0158-2 [part_number=CTB0158-2 package=THT]
  MPU6051 = female pin header, 8 pins [form="♀ (female)"]
  BME281 = female pin header, 4 pins [form="♀ (female)"]
  Q2 = MOSFET-NCHANNEL [package=to220v]
  LED1 = female pin header, 2 pins [form="♀ (female)"]
  1wire1 = female pin header, 2 pins [form="♀ (female)"]
  R3 = Resistor [tolerance=±5% resistance=6.8k package="0805 [SMD]"]
  Park1 = female alternating pin header, 3 pins [form="♀ (female)"]

nets:
  N1: WeMos_D1_Mini1.3V3, MPU6050.pin8, J6.pin8, BME280.pin4, Composant2.LV
  5V: WeMos_D1_Mini1.5V, Composant1.VCC, R1.Pin_1, J7.pin8
  N2: WeMos_D1_Mini1.A0, J6.pin2
  N3: WeMos_D1_Mini1.D0, J6.pin3
  N4: WeMos_D1_Mini1.D1, Composant1.XCL, MPU6050.pin5, J7.pin3, BME280.pin1
  N5: WeMos_D1_Mini1.D2, Composant1.XDA, MPU6050.pin6, J7.pin4, BME280.pin2
  N6: WeMos_D1_Mini1.D3, Composant1.SDA, J7.pin5
  N7: WeMos_D1_Mini1.D4, Composant1.SCL, J7.pin6, LED.pin1
  N8: WeMos_D1_Mini1.D5, J6.pin4, Q1.G
  N9: WeMos_D1_Mini1.D6, J6.pin5, Composant2.TX2_LV
  N10: WeMos_D1_Mini1.D7, J6.pin6, Composant2.RX2_LV
  N11: WeMos_D1_Mini1.D8, J6.pin7
  GND: WeMos_D1_Mini1.G, Composant1.GND, Alimentation_5_0_12V.pin2, 12V_caméra.pin1, 1wire.pin1, MPU6050.pin7, J7.pin7, BME280.pin3, LED.pin2, Q1.S, Composant2.GND
  N12: WeMos_D1_Mini1.RST, J6.pin1
  N13: WeMos_D1_Mini1.RX, Composant1.AD0, J7.pin2
  N14: WeMos_D1_Mini1.TX, Composant1.INT, J7.pin1
  N15: Alimentation_5_0_12V.pin3, 12V_caméra.pin2, 12V_chauffage.pin1
  N16: 12V_chauffage.pin2, Q1.D
  N17: 1wire.pin2, R1.Pin_0, Composant2.RX2_HV
  N18: Park.pin1, R2.Pin_1, Composant3.GND, Composant3.D6, MPU6051.pin7, BME281.pin3, Q2.S, LED1.pin1, 1wire1.pin1, Park1.pin1
  N19: Park.pin2, Composant3.5V, Composant3.A3, MPU6051.pin8, BME281.pin4, R3.Pin_0, Park1.pin3
  N20: Park.pin3, Composant3.D9
  N21: R2.Pin_0, Composant3.D11/MOSI, Q2.G
  N22: Composant3.D2, 1wire1.pin2, R3.Pin_1
  N23: Composant3.D7, Park1.pin2
  N24: Composant3.D12/MISO, LED1.pin2
  N25: Composant3.A6, Composant3.A4, MPU6051.pin5, BME281.pin1
  N26: Composant3.A5, MPU6051.pin6, BME281.pin2
  N27: Alimentation_5_0_12V1.pin2, 12V_caméra1.pin1
  N28: Alimentation_5_0_12V1.pin3, 12V_chauffage1.pin1, 12V_caméra1.pin2
  N29: 12V_chauffage1.pin2, Q2.D

custom parts:
  WeMos D1 Mini: The D1 mini is a mini wifi board based on ESP-8266EX.
