# Fritzing sketch AntiBueeNano2 (saved by Fritzing 0.9.3b)
stripboards: 2

parts:
  R2 = Resistor [tolerance=±5% resistance=1k package="0805 [SMD]"]
  Composant3 = Arduino Nano (Rev3.0) (ICSP)
  12V_caméra = Camdenboss CTB0158-2 [part_number=CTB0158-2 package=THT]
  MPU6050 = female pin header, 8 pins [form="♀ (female)"]
  BME280 = female pin header, 4 pins [form="♀ (female)"]
  Q2 = MOSFET-NCHANNEL [package=to220v]
  R3 = Resistor [tolerance=±5% resistance=6.8k package="0805 [SMD]"]
  Composant1 = InvenSense MPU6050  # not connected
  Alimentation_5-0-Park-12V = shrouded pin header, 8 pins [form="♂ (shrouded male)"]
  LED = female pin header, 3 pins [form="♀ (female)"]
  gnd-1wire-chauff = shrouded pin header, 8 pins [form="♂ (shrouded male)"]
  Alimentation_focuser = shrouded pin header, 8 pins [form="♂ (shrouded male)"]
  DHT22 = female pin header, 3 pins [form="♀ (female)"]
  Serial = single row smd female pin header, 4 pins [form="♀ (female)"]
  WeMos_D1_Mini1 = WeMos D1 Mini
  BME281 = male pin header, 4 pins [form="♂ (male)"]
  Wemos = single row smd female pin header, 6 pins [form="♀ (female)"]
  BME282 = male pin header, 6 pins [form="♂ (male)"]
  BME283 = female pin header, 8 pins [form="♀ (female)"]
  BME284 = female pin header, 8 pins [form="♀ (female)"]
  Wemos1 = single row smd female pin header, 3 pins [form="♀ (female)"]
  BME285 = male pin header, 3 pins [form="♂ (male)"]  # not connected

nets:
  N1: R2.Pin_0, Composant3.D11/MOSI, Q2.G
  N2: R2.Pin_1, Composant3.GND, 12V_caméra.pin1, MPU6050.pin7, BME280.pin3, Q2.S, Alimentation_5-0-Park-12V.pin2, Alimentation_5-0-Park-12V.pin7, LED.pin3, gnd-1wire-chauff.pin4, gnd-1wire-chauff.pin5, Alimentation_focuser.pin2, Alimentation_focuser.pin7, DHT22.pin2, Serial.pin4
  N3: Composant3.D1/TX, Serial.pin2
  N4: Composant3.D0/RX, Serial.pin3
  N5: Composant3.D2, R3.Pin_1, gnd-1wire-chauff.pin3, gnd-1wire-chauff.pin6
  N6: Composant3.D9, LED.pin1
  N7: Composant3.D12/MISO, DHT22.pin3
  N8: Composant3.VIN, Wemos.pin2
  N9: Composant3.5V, MPU6050.pin8, BME280.pin4, R3.Pin_0, Alimentation_5-0-Park-12V.pin1, Alimentation_5-0-Park-12V.pin8, LED.pin2, Alimentation_focuser.pin1, Alimentation_focuser.pin8, DHT22.pin1, Serial.pin1, Wemos.pin1, Wemos1.pin1
  N10: Composant3.A5, MPU6050.pin6, BME280.pin2
  N11: Composant3.A4, MPU6050.pin5, BME280.pin1
  N12: Composant3.A2, Wemos1.pin2
  N13: Composant3.A1, Wemos1.pin3
  N14: Composant3.A0, Alimentation_5-0-Park-12V.pin3, Alimentation_5-0-Park-12V.pin6, Alimentation_focuser.pin3, Alimentation_focuser.pin6
  N15: 12V_caméra.pin2, Alimentation_5-0-Park-12V.pin4, Alimentation_5-0-Park-12V.pin5, gnd-1wire-chauff.pin2, gnd-1wire-chauff.pin7, Alimentation_focuser.pin4, Alimentation_focuser.pin5
  N16: Q2.D, gnd-1wire-chauff.pin1, gnd-1wire-chauff.pin8
  N17: WeMos_D1_Mini1.3V3, BME284.pin1
  N18: WeMos_D1_Mini1.5V, BME281.pin1, BME282.pin1, BME283.pin1
  N19: WeMos_D1_Mini1.A0, BME284.pin7
  N20: WeMos_D1_Mini1.D0, BME284.pin6
  N21: WeMos_D1_Mini1.D1, BME283.pin6
  N22: WeMos_D1_Mini1.D2, BME283.pin5
  N23: WeMos_D1_Mini1.D3, BME283.pin4
  N24: WeMos_D1_Mini1.D4, BME283.pin3
  N25: WeMos_D1_Mini1.D5, BME284.pin5
  N26: WeMos_D1_Mini1.D6, BME284.pin4
  N27: WeMos_D1_Mini1.D7, BME284.pin3
  N28: WeMos_D1_Mini1.D8, BME284.pin2
  N29: WeMos_D1_Mini1.G, BME281.pin4, BME283.pin2
  N30: WeMos_D1_Mini1.RST, BME284.pin8
  N31: WeMos_D1_Mini1.RX, BME281.pin2, BME283.pin7
  N32: WeMos_D1_Mini1.TX, BME281.pin3, BME283.pin8

custom parts:
  WeMos D1 Mini: The D1 mini is a mini wifi board based on ESP-8266EX.
